# Fritzing sketch Capture_and_Transmit_Circuit_layout (saved by Fritzing 1.0.0rc)

parts:
  M1 = Osoyoo SX1278-ra-02
  Part1 = Arduino Nano (Rev3.0) (ICSP)
  A1 = u-blox NEO-6M GPS Breakout
  Part2 = InvenSense MPU6050
  Part3 = GY-BMEP280 Barometric Pressure Sensor - Breakout
  Bat1 = battery_holder_single_18650
  S1 = Momentary Switch 6mm 2pin

nets:
  GND: M1.GND, Part1.GND, A1.Pin_2, Part2.GND, Part3.GND, Bat1.+#1
  VCC: M1.3.3V, Part1.3V3, Part2.VCC, Part3.VCC
  N1: M1.SCK, Part1.D13/SCK
  N2: M1.MISO, Part1.D12/MISO
  N3: M1.MOSI, Part1.D11/MOSI
  N4: M1.NSS, Part1.D10
  N5: Part1.D5, A1.Pin_3
  N6: Part1.D6, A1.Pin_4
  N7: Part1.VIN, S1.2
  N8: Part1.5V, A1.Pin_1
  N9: Part1.A5, Part2.SCL, Part3.SCL
  N10: Part1.A4, Part2.SDA, Part3.SDA
  N11: Bat1.+#0, S1.1

notes:
  NEO7M GPS
  MPU6050
  BMP280
  Ra-02-SX1278 LoRa
  3.7V Power supply

custom parts:
  Osoyoo SX1278-ra-02: Osoyoo Long Distance wireless transceiver Uart LoRa Module.
  GY-BMEP280 Barometric Pressure Sensor - Breakout: The BME280 is a chip which was originally designed for the next generation of smartphones. It is made up of a very accurate pressure sensor and an associated temperature sensor which helps calibrate the pressure readings. And just for fun they threw in a pretty solid humidity sensor in there as well! So with an I2C connection you have access to enough weather data to make some pretty good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
  battery_holder_single_18650: single 18650 battery holder
  Momentary Switch 6mm 2pin: Momentary Switch 6mm 2 pin Button commonly used for reset or general input.
