# Fritzing sketch Receive and Display Circuit_layout (saved by Fritzing 1.0.0rc)

parts:
  CPU2 = NodeMCU WROOM ESP 32
  M2 = Osoyoo SX1278-ra-02
  OLED_I2C2 = OLED 128x64 I2C Monochrome Display
  Bat1 = battery_holder_single_18650
  S1 = Momentary Switch 6mm 2pin

nets:
  N1: CPU2.pin_15, Bat1.+#1
  N2: CPU2.pin_16, S1.2
  3.3V: CPU2.pin_17, M2.3.3V, OLED_I2C2.VDD
  GND: CPU2.pin_18, CPU2.pin_24, M2.GND, M2.NSS, OLED_I2C2.GND
  N3: CPU2.pin_25, M2.SCK
  N4: CPU2.pin_26, M2.MISO
  N5: CPU2.pin_27, OLED_I2C2.SDA
  N6: CPU2.pin_30, OLED_I2C2.SCK
  N7: CPU2.pin_31, M2.MOSI
  N8: Bat1.+#0, S1.1

notes:
  RA-02-SX1278 LoRa Module
  124X68 OLED
  3.7V Power supply

custom parts:
  NodeMCU WROOM ESP 32: 30 pol Development Kit
  Osoyoo SX1278-ra-02: Osoyoo Long Distance wireless transceiver Uart LoRa Module.
  battery_holder_single_18650: single 18650 battery holder
  Momentary Switch 6mm 2pin: Momentary Switch 6mm 2 pin Button commonly used for reset or general input.
